# Fritzing sketch demo_photo_cell (saved by Fritzing 0.8.7b)
breadboards: 1

parts:
  R1 = Resistor [tolerance=±5% resistance=10k package=THT]
  R2 = Photocell (LDR) [package=THT]
  Part1 = Arduino Uno (Rev3)
  LED1 = LED - 5mm [color="Yellow (595nm)" package="5 mm [THT]"]
  R3 = Resistor [tolerance=±5% resistance=330 package=THT]
  R4 = Rotary Potentiometer (Small) [maximum_resistance=10kΩ package=THT]
  K1 = Relay [part_number=FRS1B-S package=THT]
  Q1 = NPN-Transistor [package="TO92 [THT]"]
  D1 = Rectifier Diode [part_number=1N4001 package="300 mil [THT]"]
  R6 = Resistor [tolerance=±5% resistance=220 package=THT]
  LED2 = RGB LED (com. cathode, rbg) [package="5 mm [THT]"]
  R7 = Resistor [tolerance=±5% resistance=2.2k package=THT]
  R8 = Resistor [tolerance=±5% resistance=220 package=THT]
  R9 = Resistor [tolerance=±5% resistance=220 package=THT]
  R11 = Resistor [tolerance=±5% resistance=10k package=THT]

nets (from the schematic view):
  N1: R1.Pin_0, R2.pin_0, Part1.A0
  GND: R1.Pin_1, Part1.GND, Q1.E
  N2: R2.pin_1, Part1.5V, R3.Pin_0, K1.C1, K1.C2, R7.Pin_1
  N3: Part1.D8, R11.Pin_0
  N4: Part1.D4, R9.Pin_0
  N5: LED1.cathode, R4.wiper
  N6: LED1.anode, R3.Pin_1
  N7: R4.leg1, LED2.common_cathode
  N8: K1.COIL1, Q1.C, D1.anode, R6.Pin_1
  N9: K1.COIL2, D1.cathode, R7.Pin_0, R8.Pin_1
  N10: Q1.B, R11.Pin_1
  N11: R6.Pin_0, LED2.red_anode
  N12: LED2.blue_anode, R8.Pin_0
  N13: LED2.green_anode, R9.Pin_1
